# Fritzing sketch palola (saved by Fritzing 0.9.9b)
perfboards: 1

parts:
  ESP8267 = NodeMCU V1.0
  HX712 = HX711 Weighing Sensor Module
  MicroUSB1 = Adafruit Micro USB Breakout [part_number="Adafruit #1833"]
  StepperDriver1 = 28BYJ-48 Driver Module [part_number=ULN2003 package=THT]
  LED2 = RGB LED (com. cathode, rgb) [package="5 mm [THT]"]
  R4 = Resistor [tolerance=±5% power=0.25 resistance=220 package=THT]
  R5 = Resistor [tolerance=±5% power=0.25 resistance=220 package=THT]
  LoadSensor1 = SEN-13329 Load Cell
  StepperMotor1 = 28BYJ-48 Stepper Motor [part_number=28BYJ-48]
  R6 = Resistor [tolerance=±5% power=0.25 resistance=220 package=THT]

nets:
  N1: ESP8267.D0, StepperDriver1.IN1
  N2: ESP8267.D1, StepperDriver1.IN2
  N3: ESP8267.D2, StepperDriver1.IN3
  N4: ESP8267.D3, StepperDriver1.IN4
  N5: ESP8267.D4, HX712.DO/RX
  GND: ESP8267.GND, HX712.GND, MicroUSB1.GND, StepperDriver1.GND, LED2.common_cathode
  N6: ESP8267.D5, HX712.CK/TX
  N7: ESP8267.D6, R4.Pin_1
  N8: ESP8267.D7, R6.Pin_1
  N9: ESP8267.D8, R5.Pin_1
  VIN: ESP8267.Vin, HX712.VCC, MicroUSB1.VBUS
  N10: HX712.E+, LoadSensor1.exc+
  N11: HX712.E-, LoadSensor1.sig+
  N12: HX712.A+, LoadSensor1.exc-
  N13: HX712.A-, LoadSensor1.sig-
  N14: StepperDriver1.blue-pin, StepperMotor1.blue-pin
  N15: StepperDriver1.pink-pin, StepperMotor1.pink-pin
  N16: StepperDriver1.yellow-pin, StepperMotor1.yellow-pin
  N17: StepperDriver1.orange-pin, StepperMotor1.orange-pin
  N18: StepperDriver1.red-pin, StepperMotor1.red-pin
  N19: LED2.red_anode, R4.Pin_0
  N20: LED2.green_anode, R6.Pin_0
  N21: LED2.blue_anode, R5.Pin_0

custom parts:
  NodeMCU V1.0: ESP8266 based NodeMCU
  Adafruit Micro USB Breakout: Simple but effective - this breakout board has a USB Micro-B connector, with all 5 pins broken out. Great for pairing with a microcontroller with USB support, or adding USB 5V power to a project. We use a micro-AB connector with through-hole shielding pads for an excellent strong connection - it won't rip off by accident! Comes with one fully assembled and tested micro B breakout PCB and a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
  28BYJ-48 Driver Module: ULN2003 Driver Module for the 28BYJ-48 Unipolar Stepper Motor LED A - Blue wire - Bottom coil left LED B - Pink wire - Top coil left LED C - Yellow wire - Bottom coil right LED D - Orange wire - Top coil right Common rail - red Connector pins: blue - pink - yellow - orange - red Control pins - IN1 to IN4 Power pins - GND & Vmotor (5-12V) On/Off jumper (if removed, power to motor is cut).
  SEN-13329 Load Cell: A Sparkfun Load Cell - 10kg, Straight Bar (TAL220) SEN-13329.
  28BYJ-48 Stepper Motor: Unipolar Stepper Motor 28BYJ-48 Top coil - pink & orange Bottom coil - blue & yellow Common rail - red Connector pins: blue - pink - yellow - orange - red
